# Fritzing sketch fritzing (saved by Fritzing 0.9.3b)
breadboards: 2

parts:
  Part1 = Photon
  R1 = Resistor [tolerance=±5% resistance=220 package="1206 [SMD]"]
  R3 = Resistor [tolerance=±5% resistance=220 package=THT]
  R4 = Resistor [tolerance=±5% resistance=220 package=THT]
  LED1 = smd LED [color="Red (633nm)" package="1206 [SMD]"]
  LED2 = smd LED [color="Red (633nm)" package="0805 [SMD]"]
  LED3 = smd LED [color="Red (633nm)" package="0805 [SMD]"]
  S1 = SWITCH-MOMENTARY-2 [package=tactile-pth]
  S2 = SWITCH-MOMENTARY-2 [package=tactile-pth]
  S3 = SWITCH-MOMENTARY-2 [package=tactile-pth]
  S4 = SWITCH-MOMENTARY-2 [package=tactile-pth]
  R5 = Resistor [tolerance=±5% resistance=220 package="1206 [SMD]"]
  R6 = Resistor [tolerance=±5% resistance=220 package="1206 [SMD]"]
  R7 = Resistor [tolerance=±5% resistance=220 package="1206 [SMD]"]
  R8 = Resistor [tolerance=±5% resistance=220 package="0805 [SMD]"]
  Part2 = Photon
  S5 = Momentary Switch [package=ksa_sealed_tac_switch]
  S6 = Momentary Switch [package=ksa_sealed_tac_switch]
  R9 = Resistor [tolerance=±5% resistance=220 package="2512 [SMD]"]
  R10 = Resistor [tolerance=±5% resistance=220 package="1206 [SMD]"]
  Grove1 = Grove OLED 128x96  # not connected

nets:
  N1: Part1.A4, R1.Pin_1
  N2: Part1.GND, LED1.cathode, LED2.cathode, LED3.cathode, R5.Pin_1, R6.Pin_1, R7.Pin_1, R8.Pin_1
  N3: Part1.D0, R4.Pin_1
  N4: Part1.D1, R3.Pin_1
  N5: Part1.D3, S4.1, R8.Pin_0
  N6: Part1.D4, S3.1, R7.Pin_0
  N7: Part1.D5, S2.1, R6.Pin_0
  N8: Part1.D6, S1.1, R5.Pin_0
  N9: Part1.3V3, S1.2, S2.2, S3.2, S4.2
  N10: R1.Pin_0, LED3.anode
  N11: R3.Pin_0, LED1.anode
  N12: R4.Pin_0, LED2.anode
  N13: Part2.GND, R9.Pin_1, R10.Pin_1
  N14: Part2.D1, S6.4, R10.Pin_0
  N15: Part2.D2, S5.4, R9.Pin_0
  N16: Part2.3V3, S5.1, S6.1

notes:
  Fault Garage Closed Open
  Closing LED, Opening LED
  Light LED
